# Fritzing sketch MONTAGE (saved by Fritzing 0.9.3b)
breadboards: 1

parts:
  Part1 = Arduino Ethernet Shield (Rev3)
  LED1 = LED - 3mm [color="Red (633nm)" package="3 mm [THT]"]
  R1 = Resistor [tolerance=±5% resistance=220 package="2010 [SMD]"]
  S2 = Pushbutton [package="[SMD]"]

nets:
  N1: Part1.GND, R1.Pin_1, S2.Pin_3, S2.Pin_4
  N2: Part1.D2, S2.Pin_1, S2.Pin_2
  N3: Part1.SDCS, LED1.anode
  N4: LED1.cathode, R1.Pin_0
